// Logisim project Laboratorio1..circ as structural Verilog: 16 circuits, main circuit Comparador1Bit
module main (
  input  [7:0] A,
  input  [7:0] E,
  input  [7:0] I,
  input  [7:0] M,
  input  [7:0] B,
  input  [7:0] F,
  input  [7:0] J,
  input  [7:0] N,
  input  [7:0] C,
  input  [7:0] G,
  input  [7:0] K,
  input  [7:0] O,
  input  [7:0] D,
  input  [7:0] H,
  input  [7:0] L,
  input  [7:0] P,
  input  in_17,
  input  in_18,
  input  in_19
);

  wire a1_t, a2, a3, a4, a5, a6, a7, a8, a9, a10, a11, a12, a13, a14, a15, a16, a17, a18, a19, a20, a21, a22,
       a23, a24, a25, a26, a27, a28, a29, a30, a31, a32, a33, a34, a35, a36, a37, a38, a39, a40, a41, a42,
       a43, a44, a45, a46, a47, a48, b1_t, b2, b3, b4, b5, b6, b7, b8, b9, b10, b11, b12, b13, b14, b15, b16,
       b17, b18, b19, b20, b21, b22, b23, b24, b25, b26, b27, b28, b29, b30, b31, b32, b33, b34, b35, b36,
       b37, b38, b39, b40, b41, b42, b43, b44, b45, b46, b47, b48, c1_t, c2, c3, c4, c5, c6, c7, c8, c9, c10,
       c11, c12, c13, c14, c15, c16, c17, c18, c19, c20, c21, c22, c23, c24, c25, c26, c27, c28, c29, c30,
       c31, c32, c33, c34, c35, c36, c37, c38, c39, c40, c41, c42, c43, c44, c45, c46, c47, c48, CLK, d1_t,
       d2, d3, d4, d5, d6, d7, d8, d9, d10, d11, d12, d13, d14, d15, d16, d17, d18, d19, d20, d21, d22, d23,
       d24, d25, d26, d27, d28, d29, d30, d31, d32, d33, d34, d35, d36, d37, d38, d39, d40, d41, d42, d43,
       d44, d45, d46, d47, d48, e1_t, e2, e3, e4, e5, e6, e7, e8, e9, e10, e11, e12, e13, e14, e15, e16, e17,
       e18, e19, e20, e21, e22, e23, e24, e25, e26, e27, e28, e29, e30, e31, e32, e33, e34, e35, e36, e37,
       e38, e39, e40, e41, e42, e43, e44, e45, e46, e47, e48, f1_t, f2, f3, f4, f5, f6, f7, f8, f9, f10, f11,
       f12, f13, f14, f15, f16, f17, f18, f19, f20, f21, f22, f23, f24, f25, f26, f27, f28, f29, f30, f31,
       f32, f33, f34, f35, f36, f37, f38, f39, f40, f41, f42, f43, f44, f45, f46, f47, f48, g1_t, g2, g3, g4,
       g5, g6, g7, g8, g9, g10, g11, g12, g13, g14, g15, g16, g17, g18, g19, g20, g21, g22, g23, g24, g25,
       g26, g27, g28, g29, g30, g31, g32, g33, g34, g35, g36, g37, g38, g39, g40, g41, g42, g43, g44, g45,
       g46, g47, g48, Resta, Resta1, Resta2, Resta3, Resta4, Resta5, Resta6, Resta7, Resta8, Resta9, Resta10,
       Resta11, Resta12, Resta13, Resta14, Resta15, Z1, Z2, Z3, Z4, Z5, Z6, Z7;
  wire [1:0] FASE;
  wire [2:0] sumar1bit_1_out_3;
  wire [7:0] A_t, B_t, C_t, D_t, E_t, F_t, G_t, H_t, I_t, J_t, K_t, L_t, M_t, N_t, O_t, P_t;
  wire [7:3] undriven;

  Clock clock_1 (.out(CLK));
  _7_Segment_Display u_7_segment_display_1 (.g(1'b1), .f(1'b1), .a(1'b1), .e(1'b1));  // open: b, d, c, dp
  _7_Segment_Display u_7_segment_display_2 (.g(1'b1), .f(1'b1), .a(1'b1), .b(1'b1), .e(1'b1), .c(1'b1));  // open: d, dp
  _7_Segment_Display u_7_segment_display_3 (.g(1'b1), .f(1'b1), .a(1'b1), .d(1'b1), .c(1'b1));  // open: b, e, dp
  _7_Segment_Display u_7_segment_display_4 (.g(1'b1), .f(1'b1), .a(1'b1), .e(1'b1), .d(1'b1));  // open: b, c, dp
  _7_Segment_Display u_7_segment_display_5 (.g(Z7), .f(Z6), .a(Z1), .b(Z2), .e(Z5), .d(Z4), .c(Z3));  // open: dp
  CompararRegistrar compararregistrar_1 (
    .A(A), .B(B), .C(C), .D(D), .E(E), .F(F), .G(G), .H(H), .I(I), .J(J), .K(K), .L(L), .M(M), .N(N), .O(O),
    .P(P), .CLK(CLK), .FASE(FASE), .out_19(A_t), .out_20(I_t), .out_21(B_t), .out_22(J_t), .out_23(C_t),
    .out_24(K_t), .out_25(D_t), .out_26(L_t), .out_27(E_t), .out_28(M_t), .out_29(F_t), .out_30(N_t),
    .out_31(G_t), .out_32(O_t), .out_33(H_t), .out_34(P_t));
  MaquinaEstados maquinaestados_1 (.X(in_19), .CLK(CLK), .CLEAR(in_18), .FASE(FASE));
  _7_Segment_Display u_7_segment_display_6 (.g(g2), .f(f2), .a(a2), .b(b2), .e(e2), .d(d2), .c(c2));  // open: dp
  _7_Segment_Display u_7_segment_display_7 (.g(g5), .f(f5), .a(a5), .b(b5), .e(e5), .d(d5), .c(c5));  // open: dp
  _7_Segment_Display u_7_segment_display_8 (.g(g8), .f(f8), .a(a8), .b(b8), .e(e8), .d(d8), .c(c8));  // open: dp
  _7_Segment_Display u_7_segment_display_9 (.g(g11), .f(f11), .a(a11), .b(b11), .e(e11), .d(d11), .c(c11));  // open: dp
  LED led_1 (.in(Resta));
  _7_Segment_Display u_7_segment_display_10 (.g(g3), .f(f3), .a(a3), .b(b3), .e(e3), .d(d3), .c(c3));  // open: dp
  _7_Segment_Display u_7_segment_display_11 (
    .g(g1_t), .f(f1_t), .a(a1_t), .b(b1_t), .e(e1_t), .d(d1_t), .c(c1_t));  // open: dp
  LED led_2 (.in(Resta1));
  _7_Segment_Display u_7_segment_display_12 (.g(g6), .f(f6), .a(a6), .b(b6), .e(e6), .d(d6), .c(c6));  // open: dp
  _7_Segment_Display u_7_segment_display_13 (.g(g4), .f(f4), .a(a4), .b(b4), .e(e4), .d(d4), .c(c4));  // open: dp
  LED led_3 (.in(Resta2));
  _7_Segment_Display u_7_segment_display_14 (.g(g9), .f(f9), .a(a9), .b(b9), .e(e9), .d(d9), .c(c9));  // open: dp
  _7_Segment_Display u_7_segment_display_15 (.g(g7), .f(f7), .a(a7), .b(b7), .e(e7), .d(d7), .c(c7));  // open: dp
  LED led_4 (.in(Resta3));
  _7_Segment_Display u_7_segment_display_16 (
    .g(g12), .f(f12), .a(a12), .b(b12), .e(e12), .d(d12), .c(c12));  // open: dp
  _7_Segment_Display u_7_segment_display_17 (
    .g(g10), .f(f10), .a(a10), .b(b10), .e(e10), .d(d10), .c(c10));  // open: dp
  _7_Segment_Display u_7_segment_display_18 (
    .g(g14), .f(f14), .a(a14), .b(b14), .e(e14), .d(d14), .c(c14));  // open: dp
  _7_Segment_Display u_7_segment_display_19 (
    .g(g17), .f(f17), .a(a17), .b(b17), .e(e17), .d(d17), .c(c17));  // open: dp
  _7_Segment_Display u_7_segment_display_20 (
    .g(g20), .f(f20), .a(a20), .b(b20), .e(e20), .d(d20), .c(c20));  // open: dp
  _7_Segment_Display u_7_segment_display_21 (
    .g(g23), .f(f23), .a(a23), .b(b23), .e(e23), .d(d23), .c(c23));  // open: dp
  LED led_5 (.in(Resta4));
  _7_Segment_Display u_7_segment_display_22 (
    .g(g15), .f(f15), .a(a15), .b(b15), .e(e15), .d(d15), .c(c15));  // open: dp
  _7_Segment_Display u_7_segment_display_23 (
    .g(g13), .f(f13), .a(a13), .b(b13), .e(e13), .d(d13), .c(c13));  // open: dp
  LED led_6 (.in(Resta5));
  _7_Segment_Display u_7_segment_display_24 (
    .g(g18), .f(f18), .a(a18), .b(b18), .e(e18), .d(d18), .c(c18));  // open: dp
  _7_Segment_Display u_7_segment_display_25 (
    .g(g16), .f(f16), .a(a16), .b(b16), .e(e16), .d(d16), .c(c16));  // open: dp
  LED led_7 (.in(Resta6));
  _7_Segment_Display u_7_segment_display_26 (
    .g(g21), .f(f21), .a(a21), .b(b21), .e(e21), .d(d21), .c(c21));  // open: dp
  _7_Segment_Display u_7_segment_display_27 (
    .g(g19), .f(f19), .a(a19), .b(b19), .e(e19), .d(d19), .c(c19));  // open: dp
  LED led_8 (.in(Resta7));
  _7_Segment_Display u_7_segment_display_28 (
    .g(g24), .f(f24), .a(a24), .b(b24), .e(e24), .d(d24), .c(c24));  // open: dp
  _7_Segment_Display u_7_segment_display_29 (
    .g(g22), .f(f22), .a(a22), .b(b22), .e(e22), .d(d22), .c(c22));  // open: dp
  _7_Segment_Display u_7_segment_display_30 (
    .g(g26), .f(f26), .a(a26), .b(b26), .e(e26), .d(d26), .c(c26));  // open: dp
  _7_Segment_Display u_7_segment_display_31 (
    .g(g29), .f(f29), .a(a29), .b(b29), .e(e29), .d(d29), .c(c29));  // open: dp
  _7_Segment_Display u_7_segment_display_32 (
    .g(g32), .f(f32), .a(a32), .b(b32), .e(e32), .d(d32), .c(c32));  // open: dp
  _7_Segment_Display u_7_segment_display_33 (
    .g(g35), .f(f35), .a(a35), .b(b35), .e(e35), .d(d35), .c(c35));  // open: dp
  LED led_9 (.in(Resta8));
  _7_Segment_Display u_7_segment_display_34 (
    .g(g27), .f(f27), .a(a27), .b(b27), .e(e27), .d(d27), .c(c27));  // open: dp
  _7_Segment_Display u_7_segment_display_35 (
    .g(g25), .f(f25), .a(a25), .b(b25), .e(e25), .d(d25), .c(c25));  // open: dp
  LED led_10 (.in(Resta9));
  _7_Segment_Display u_7_segment_display_36 (
    .g(g30), .f(f30), .a(a30), .b(b30), .e(e30), .d(d30), .c(c30));  // open: dp
  _7_Segment_Display u_7_segment_display_37 (
    .g(g28), .f(f28), .a(a28), .b(b28), .e(e28), .d(d28), .c(c28));  // open: dp
  LED led_11 (.in(Resta10));
  _7_Segment_Display u_7_segment_display_38 (
    .g(g33), .f(f33), .a(a33), .b(b33), .e(e33), .d(d33), .c(c33));  // open: dp
  _7_Segment_Display u_7_segment_display_39 (
    .g(g31), .f(f31), .a(a31), .b(b31), .e(e31), .d(d31), .c(c31));  // open: dp
  LED led_12 (.in(Resta11));
  _7_Segment_Display u_7_segment_display_40 (
    .g(g36), .f(f36), .a(a36), .b(b36), .e(e36), .d(d36), .c(c36));  // open: dp
  _7_Segment_Display u_7_segment_display_41 (
    .g(g34), .f(f34), .a(a34), .b(b34), .e(e34), .d(d34), .c(c34));  // open: dp
  _7_Segment_Display u_7_segment_display_42 (
    .g(g38), .f(f38), .a(a38), .b(b38), .e(e38), .d(d38), .c(c38));  // open: dp
  _7_Segment_Display u_7_segment_display_43 (
    .g(g41), .f(f41), .a(a41), .b(b41), .e(e41), .d(d41), .c(c41));  // open: dp
  _7_Segment_Display u_7_segment_display_44 (
    .g(g44), .f(f44), .a(a44), .b(b44), .e(e44), .d(d44), .c(c44));  // open: dp
  _7_Segment_Display u_7_segment_display_45 (
    .g(g47), .f(f47), .a(a47), .b(b47), .e(e47), .d(d47), .c(c47));  // open: dp
  LED led_13 (.in(Resta12));
  _7_Segment_Display u_7_segment_display_46 (
    .g(g39), .f(f39), .a(a39), .b(b39), .e(e39), .d(d39), .c(c39));  // open: dp
  _7_Segment_Display u_7_segment_display_47 (
    .g(g37), .f(f37), .a(a37), .b(b37), .e(e37), .d(d37), .c(c37));  // open: dp
  LED led_14 (.in(Resta13));
  _7_Segment_Display u_7_segment_display_48 (
    .g(g42), .f(f42), .a(a42), .b(b42), .e(e42), .d(d42), .c(c42));  // open: dp
  _7_Segment_Display u_7_segment_display_49 (
    .g(g40), .f(f40), .a(a40), .b(b40), .e(e40), .d(d40), .c(c40));  // open: dp
  LED led_15 (.in(Resta14));
  _7_Segment_Display u_7_segment_display_50 (
    .g(g45), .f(f45), .a(a45), .b(b45), .e(e45), .d(d45), .c(c45));  // open: dp
  _7_Segment_Display u_7_segment_display_51 (
    .g(g43), .f(f43), .a(a43), .b(b43), .e(e43), .d(d43), .c(c43));  // open: dp
  LED led_16 (.in(Resta15));
  _7_Segment_Display u_7_segment_display_52 (
    .g(g48), .f(f48), .a(a48), .b(b48), .e(e48), .d(d48), .c(c48));  // open: dp
  _7_Segment_Display u_7_segment_display_53 (
    .g(g46), .f(f46), .a(a46), .b(b46), .e(e46), .d(d46), .c(c46));  // open: dp
  DisplaySegmentos displaysegmentos_1 (
    .in_1(A_t), .a2(a2), .b2(b2), .c2(c2), .Resta(Resta), .d2(d2), .e2(e2), .f2(f2), .g2(g2), .a1(a1_t),
    .b1(b1_t), .c1(c1_t), .d1(d1_t), .a3(a3), .e1(e1_t), .b3(b3), .f1(f1_t), .c3(c3), .g1(g1_t), .d3(d3),
    .e3(e3), .f3(f3), .g3(g3));
  DisplaySegmentos displaysegmentos_2 (
    .in_1(B_t), .a2(a5), .b2(b5), .c2(c5), .Resta(Resta1), .d2(d5), .e2(e5), .f2(f5), .g2(g5), .a1(a4),
    .b1(b4), .c1(c4), .d1(d4), .a3(a6), .e1(e4), .b3(b6), .f1(f4), .c3(c6), .g1(g4), .d3(d6), .e3(e6),
    .f3(f6), .g3(g6));
  DisplaySegmentos displaysegmentos_3 (
    .in_1(C_t), .a2(a8), .b2(b8), .c2(c8), .Resta(Resta2), .d2(d8), .e2(e8), .f2(f8), .g2(g8), .a1(a7),
    .b1(b7), .c1(c7), .d1(d7), .a3(a9), .e1(e7), .b3(b9), .f1(f7), .c3(c9), .g1(g7), .d3(d9), .e3(e9),
    .f3(f9), .g3(g9));
  DisplaySegmentos displaysegmentos_4 (
    .in_1(D_t), .a2(a11), .b2(b11), .c2(c11), .Resta(Resta3), .d2(d11), .e2(e11), .f2(f11), .g2(g11),
    .a1(a10), .b1(b10), .c1(c10), .d1(d10), .a3(a12), .e1(e10), .b3(b12), .f1(f10), .c3(c12), .g1(g10),
    .d3(d12), .e3(e12), .f3(f12), .g3(g12));
  DisplaySegmentos displaysegmentos_5 (
    .in_1(E_t), .a2(a14), .b2(b14), .c2(c14), .Resta(Resta4), .d2(d14), .e2(e14), .f2(f14), .g2(g14),
    .a1(a13), .b1(b13), .c1(c13), .d1(d13), .a3(a15), .e1(e13), .b3(b15), .f1(f13), .c3(c15), .g1(g13),
    .d3(d15), .e3(e15), .f3(f15), .g3(g15));
  DisplaySegmentos displaysegmentos_6 (
    .in_1(F_t), .a2(a17), .b2(b17), .c2(c17), .Resta(Resta5), .d2(d17), .e2(e17), .f2(f17), .g2(g17),
    .a1(a16), .b1(b16), .c1(c16), .d1(d16), .a3(a18), .e1(e16), .b3(b18), .f1(f16), .c3(c18), .g1(g16),
    .d3(d18), .e3(e18), .f3(f18), .g3(g18));
  DisplaySegmentos displaysegmentos_7 (
    .in_1(G_t), .a2(a20), .b2(b20), .c2(c20), .Resta(Resta6), .d2(d20), .e2(e20), .f2(f20), .g2(g20),
    .a1(a19), .b1(b19), .c1(c19), .d1(d19), .a3(a21), .e1(e19), .b3(b21), .f1(f19), .c3(c21), .g1(g19),
    .d3(d21), .e3(e21), .f3(f21), .g3(g21));
  DisplaySegmentos displaysegmentos_8 (
    .in_1(H_t), .a2(a23), .b2(b23), .c2(c23), .Resta(Resta7), .d2(d23), .e2(e23), .f2(f23), .g2(g23),
    .a1(a22), .b1(b22), .c1(c22), .d1(d22), .a3(a24), .e1(e22), .b3(b24), .f1(f22), .c3(c24), .g1(g22),
    .d3(d24), .e3(e24), .f3(f24), .g3(g24));
  DisplaySegmentos displaysegmentos_9 (
    .in_1(I_t), .a2(a26), .b2(b26), .c2(c26), .Resta(Resta8), .d2(d26), .e2(e26), .f2(f26), .g2(g26),
    .a1(a25), .b1(b25), .c1(c25), .d1(d25), .a3(a27), .e1(e25), .b3(b27), .f1(f25), .c3(c27), .g1(g25),
    .d3(d27), .e3(e27), .f3(f27), .g3(g27));
  DisplaySegmentos displaysegmentos_10 (
    .in_1(J_t), .a2(a29), .b2(b29), .c2(c29), .Resta(Resta9), .d2(d29), .e2(e29), .f2(f29), .g2(g29),
    .a1(a28), .b1(b28), .c1(c28), .d1(d28), .a3(a30), .e1(e28), .b3(b30), .f1(f28), .c3(c30), .g1(g28),
    .d3(d30), .e3(e30), .f3(f30), .g3(g30));
  DisplaySegmentos displaysegmentos_11 (
    .in_1(K_t), .a2(a32), .b2(b32), .c2(c32), .Resta(Resta10), .d2(d32), .e2(e32), .f2(f32), .g2(g32),
    .a1(a31), .b1(b31), .c1(c31), .d1(d31), .a3(a33), .e1(e31), .b3(b33), .f1(f31), .c3(c33), .g1(g31),
    .d3(d33), .e3(e33), .f3(f33), .g3(g33));
  DisplaySegmentos displaysegmentos_12 (
    .in_1(L_t), .a2(a35), .b2(b35), .c2(c35), .Resta(Resta11), .d2(d35), .e2(e35), .f2(f35), .g2(g35),
    .a1(a34), .b1(b34), .c1(c34), .d1(d34), .a3(a36), .e1(e34), .b3(b36), .f1(f34), .c3(c36), .g1(g34),
    .d3(d36), .e3(e36), .f3(f36), .g3(g36));
  DisplaySegmentos displaysegmentos_13 (
    .in_1(M_t), .a2(a38), .b2(b38), .c2(c38), .Resta(Resta12), .d2(d38), .e2(e38), .f2(f38), .g2(g38),
    .a1(a37), .b1(b37), .c1(c37), .d1(d37), .a3(a39), .e1(e37), .b3(b39), .f1(f37), .c3(c39), .g1(g37),
    .d3(d39), .e3(e39), .f3(f39), .g3(g39));
  DisplaySegmentos displaysegmentos_14 (
    .in_1(N_t), .a2(a41), .b2(b41), .c2(c41), .Resta(Resta13), .d2(d41), .e2(e41), .f2(f41), .g2(g41),
    .a1(a40), .b1(b40), .c1(c40), .d1(d40), .a3(a42), .e1(e40), .b3(b42), .f1(f40), .c3(c42), .g1(g40),
    .d3(d42), .e3(e42), .f3(f42), .g3(g42));
  DisplaySegmentos displaysegmentos_15 (
    .in_1(O_t), .a2(a44), .b2(b44), .c2(c44), .Resta(Resta14), .d2(d44), .e2(e44), .f2(f44), .g2(g44),
    .a1(a43), .b1(b43), .c1(c43), .d1(d43), .a3(a45), .e1(e43), .b3(b45), .f1(f43), .c3(c45), .g1(g43),
    .d3(d45), .e3(e45), .f3(f45), .g3(g45));
  DisplaySegmentos displaysegmentos_16 (
    .in_1(P_t), .a2(a47), .b2(b47), .c2(c47), .Resta(Resta15), .d2(d47), .e2(e47), .f2(f47), .g2(g47),
    .a1(a46), .b1(b46), .c1(c46), .d1(d46), .a3(a48), .e1(e46), .b3(b48), .f1(f46), .c3(c48), .g1(g46),
    .d3(d48), .e3(e48), .f3(f48), .g3(g48));
  Sumar1Bit sumar1bit_1 (.FASE(FASE), .Sumar1(in_17), .out_3(sumar1bit_1_out_3));
  DisplaySegmentos displaysegmentos_17 (
    .in_1({undriven, sumar1bit_1_out_3}), .a1(Z1), .b1(Z2), .c1(Z3), .d1(Z4), .e1(Z5), .f1(Z6), .g1(Z7));  // open: a2, b2, c2, Resta, d2, e2, f2, g2, a3, b3, c3, d3, e3, f3, g3

  // Other names for the same wires on the sheet: A1[7:0] = A; ACTIVARFASES = in_17; B1[7:0] = B; C1[7:0] = C;
  //   CLEAR = in_18; D1[7:0] = D; E1[7:0] = E; F1[7:0] = F; G1[7:0] = G; H1[7:0] = H; I1[7:0] = I; INGRESAR1 = in_19;
  //   J1[7:0] = J; K1[7:0] = K; L1[7:0] = L; M1[7:0] = M; N1[7:0] = N; O1[7:0] = O; P1[7:0] = P
endmodule

module Comparador1Bit (
  input  P1,
  input  P0,
  input  D1,
  input  D0,
  output C1,
  output C0
);

  wire and_1_out, and_2_out;

  and and_1 (and_1_out, ~P0, D1, ~D0);  // AND_Gate
  and and_2 (and_2_out, ~P1, D0, ~D1);  // AND_Gate
  or or_1 (C1, and_1_out, P1);
  or or_2 (C0, and_2_out, P0);
endmodule

module Comparador1BitSigno (
  input  P1,
  input  P0,
  output C1,
  output C0
);

  and and_1 (C1, ~P1, P0);  // AND_Gate
  and and_2 (C0, ~P0, P1);  // AND_Gate
endmodule

module Comparador8Bits (
  input  A7,
  input  A6,
  input  A5,
  input  A4,
  input  A3,
  input  A2,
  input  A1,
  input  A0,
  input  B7,
  input  B6,
  input  B5,
  input  B4,
  input  B3,
  input  B2,
  input  B1,
  input  B0,
  output C1,
  output C0
);

  wire comparador1bit_1_c0, comparador1bit_1_c1, comparador1bit_2_c0, comparador1bit_2_c1,
       comparador1bit_3_c0, comparador1bit_3_c1, comparador1bit_4_c0, comparador1bit_4_c1,
       comparador1bit_5_c0, comparador1bit_5_c1, comparador1bit_6_c0, comparador1bit_6_c1,
       comparador1bitsigno_1_c0, comparador1bitsigno_1_c1;

  Comparador1BitSigno comparador1bitsigno_1 (
    .P1(A7), .P0(B7), .C1(comparador1bitsigno_1_c1), .C0(comparador1bitsigno_1_c0));
  Comparador1Bit comparador1bit_1 (
    .P1(comparador1bitsigno_1_c1), .P0(comparador1bitsigno_1_c0), .D1(A6), .D0(B6), .C1(comparador1bit_1_c1),
    .C0(comparador1bit_1_c0));
  Comparador1Bit comparador1bit_2 (
    .P1(comparador1bit_1_c1), .P0(comparador1bit_1_c0), .D1(A5), .D0(B5), .C1(comparador1bit_2_c1),
    .C0(comparador1bit_2_c0));
  Comparador1Bit comparador1bit_3 (
    .P1(comparador1bit_2_c1), .P0(comparador1bit_2_c0), .D1(A4), .D0(B4), .C1(comparador1bit_3_c1),
    .C0(comparador1bit_3_c0));
  Comparador1Bit comparador1bit_4 (
    .P1(comparador1bit_3_c1), .P0(comparador1bit_3_c0), .D1(A3), .D0(B3), .C1(comparador1bit_4_c1),
    .C0(comparador1bit_4_c0));
  Comparador1Bit comparador1bit_5 (
    .P1(comparador1bit_4_c1), .P0(comparador1bit_4_c0), .D1(A2), .D0(B2), .C1(comparador1bit_5_c1),
    .C0(comparador1bit_5_c0));
  Comparador1Bit comparador1bit_6 (
    .P1(comparador1bit_5_c1), .P0(comparador1bit_5_c0), .D1(A1), .D0(B1), .C1(comparador1bit_6_c1),
    .C0(comparador1bit_6_c0));
  Comparador1Bit comparador1bit_7 (
    .P1(comparador1bit_6_c1), .P0(comparador1bit_6_c0), .D1(A0), .D0(B0), .C1(C1), .C0(C0));
endmodule

module Comparador (
  input  [7:0] in_1,
  input  [7:0] in_2,
  output [7:0] out_3,
  output [7:0] out_4
);

  wire comparador8bits_1_c0, comparador8bits_1_c1;

  Comparador8Bits comparador8bits_1 (
    .A7(in_1[7]), .A6(in_1[6]), .A5(in_1[5]), .A4(in_1[4]), .A3(in_1[3]), .A2(in_1[2]), .A1(in_1[1]),
    .A0(in_1[0]), .B7(in_2[7]), .B6(in_2[6]), .B5(in_2[5]), .B4(in_2[4]), .B3(in_2[3]), .B2(in_2[2]),
    .B1(in_2[1]), .B0(in_2[0]), .C1(comparador8bits_1_c1), .C0(comparador8bits_1_c0));
  Multiplexer #(.width(8)) multiplexer_1 (.in0(in_1), .in1(in_2), .out(out_3), .sel(comparador8bits_1_c0));
  Multiplexer #(.width(8)) multiplexer_2 (.in0(in_1), .in1(in_2), .out(out_4), .sel(comparador8bits_1_c1));

  // Other names for the same wires on the sheet: A[7:0] = in_1; B[7:0] = in_2
endmodule

module BCD4X8 (
  input  [7:0] numero,
  input  [7:0] divisor,
  output [7:0] decuni,
  output [7:0] unisigno
);

  wire [7:0] adder_1_out, adder_2_out, divider_1_out, divider_1_rem, not_1_out, not_2_out;

  // Probe on numero
  // Probe on divisor
  Divider #(.mode("twosComplement")) divider_1 (
    .a(numero), .b(divisor), .out(divider_1_out), .rem(divider_1_rem));  // open: upper
  // Probe on divider_1_rem
  // Probe on divider_1_out
  assign not_1_out = ~divider_1_rem;  // NOT_Gate not_1, 8 bits wide
  Adder adder_1 (.a(not_1_out), .b(8'h1), .out(adder_1_out));  // open: cin, cout
  assign not_2_out = ~divider_1_out;  // NOT_Gate not_2, 8 bits wide
  Adder adder_2 (.a(not_2_out), .b(8'h1), .out(adder_2_out));  // open: cin, cout
  Multiplexer #(.width(8)) multiplexer_1 (
    .in0(divider_1_rem), .in1(adder_1_out), .out(unisigno), .sel(divider_1_rem[7]));
  Multiplexer #(.width(8)) multiplexer_2 (.in0(divider_1_out), .in1(adder_2_out), .out(decuni), .sel(divider_1_out[7]));
endmodule

module SieteSegmentos (
  input  W,
  input  X,
  input  Y,
  input  Z,
  output a,
  output b,
  output c,
  output d,
  output e,
  output f,
  output g
);

  wire and_1_out, and_2_out, and_3_out, and_4_out, and_5_out, and_6_out, and_7_out, and_8_out, and_9_out,
       and_10_out, and_11_out, and_12_out, and_13_out, and_14_out, and_15_out, and_16_out, not_1_out,
       not_2_out, not_3_out;

  not not_1 (not_1_out, X);
  not not_2 (not_2_out, Y);
  not not_3 (not_3_out, Z);
  and and_1 (and_1_out, not_1_out, not_3_out);
  and and_2 (and_2_out, X, Z);
  and and_3 (and_3_out, not_2_out, not_3_out);
  and and_4 (and_4_out, Y, Z);
  or or_1 (c, not_2_out, Z, X);
  and and_5 (and_5_out, not_1_out, not_3_out);
  and and_6 (and_6_out, not_1_out, Y);
  and and_7 (and_7_out, Y, not_3_out);
  and and_8 (and_8_out, X, not_2_out, Z);
  and and_9 (and_9_out, not_1_out, not_3_out);
  and and_10 (and_10_out, Y, not_3_out);
  and and_11 (and_11_out, not_2_out, not_3_out);
  and and_12 (and_12_out, X, not_2_out);
  and and_13 (and_13_out, X, not_3_out);
  and and_14 (and_14_out, not_1_out, Y);
  and and_15 (and_15_out, X, not_2_out);
  and and_16 (and_16_out, X, not_3_out);
  or or_2 (a, and_1_out, Y, and_2_out, W);
  or or_3 (b, not_1_out, and_3_out, and_4_out);
  or or_4 (d, and_5_out, and_6_out, and_7_out, and_8_out);
  or or_5 (e, and_9_out, and_10_out);
  or or_6 (f, and_11_out, and_12_out, and_13_out, W);
  or or_7 (g, and_14_out, and_15_out, and_16_out, W);
endmodule

module DisplaySegmentos (
  input  [7:0] in_1,
  output a2,
  output b2,
  output c2,
  output Resta,
  output d2,
  output e2,
  output f2,
  output g2,
  output a1,
  output b1,
  output c1,
  output d1,
  output a3,
  output e1,
  output b3,
  output f1,
  output c3,
  output g1,
  output d3,
  output e3,
  output f3,
  output g3
);

  wire [7:0] bcd4x8_1_decuni, bcd4x8_1_unisigno, bcd4x8_2_decuni, bcd4x8_2_unisigno;

  // Probe on bcd4x8_2_unisigno
  // Probe on in_1
  // Probe on bcd4x8_1_decuni
  BCD4X8 bcd4x8_1 (.numero(in_1), .divisor(8'h64), .decuni(bcd4x8_1_decuni), .unisigno(bcd4x8_1_unisigno));
  SieteSegmentos sietesegmentos_1 (
    .W(bcd4x8_2_unisigno[3]), .X(bcd4x8_2_unisigno[2]), .Y(bcd4x8_2_unisigno[1]), .Z(bcd4x8_2_unisigno[0]),
    .a(a1), .b(b1), .c(c1), .d(d1), .e(e1), .f(f1), .g(g1));
  // Probe on bcd4x8_2_decuni
  BCD4X8 bcd4x8_2 (.numero(bcd4x8_1_unisigno), .divisor(8'ha), .decuni(bcd4x8_2_decuni), .unisigno(bcd4x8_2_unisigno));
  SieteSegmentos sietesegmentos_2 (
    .W(bcd4x8_1_decuni[3]), .X(bcd4x8_1_decuni[2]), .Y(bcd4x8_1_decuni[1]), .Z(bcd4x8_1_decuni[0]), .a(a2),
    .b(b2), .c(c2), .d(d2), .e(e2), .f(f2), .g(g2));
  SieteSegmentos sietesegmentos_3 (
    .W(bcd4x8_2_decuni[3]), .X(bcd4x8_2_decuni[2]), .Y(bcd4x8_2_decuni[1]), .Z(bcd4x8_2_decuni[0]), .a(a3),
    .b(b3), .c(c3), .d(d3), .e(e3), .f(f3), .g(g3));

  assign Resta = in_1[7];
endmodule

module Registro1Bit (
  input  D,
  input  CLK,
  output out_3
);

  wire not_1_out;

  S_R_Flip_Flop s_r_ff_1 (.S(D), .R(not_1_out), .clk(CLK), .Q(out_3));  // open: reset, Qn, preset
  not not_1 (not_1_out, D);
endmodule

module Registro8Bits (
  input  [7:0] NumReg,
  input  CLK,
  output [7:0] out_3
);

  Registro1Bit registro1bit_1 (.D(NumReg[0]), .CLK(CLK), .out_3(out_3[0]));
  Registro1Bit registro1bit_2 (.D(NumReg[1]), .CLK(CLK), .out_3(out_3[1]));
  Registro1Bit registro1bit_3 (.D(NumReg[2]), .CLK(CLK), .out_3(out_3[2]));
  Registro1Bit registro1bit_4 (.D(NumReg[3]), .CLK(CLK), .out_3(out_3[3]));
  Registro1Bit registro1bit_5 (.D(NumReg[4]), .CLK(CLK), .out_3(out_3[4]));
  Registro1Bit registro1bit_6 (.D(NumReg[5]), .CLK(CLK), .out_3(out_3[5]));
  Registro1Bit registro1bit_7 (.D(NumReg[6]), .CLK(CLK), .out_3(out_3[6]));
  Registro1Bit registro1bit_8 (.D(NumReg[7]), .CLK(CLK), .out_3(out_3[7]));
endmodule

module Comparar16Num (
  input  [7:0] A,
  input  [7:0] B,
  input  [7:0] C,
  input  [7:0] D,
  input  [7:0] E,
  input  [7:0] F,
  input  [7:0] G,
  input  [7:0] H,
  input  [7:0] I,
  input  [7:0] J,
  input  [7:0] K,
  input  [7:0] L,
  input  [7:0] M,
  input  [7:0] N,
  input  [7:0] O,
  input  [7:0] P,
  output [7:0] out_17,
  output [7:0] out_18,
  output [7:0] out_19,
  output [7:0] out_20,
  output [7:0] out_21,
  output [7:0] out_22,
  output [7:0] out_23,
  output [7:0] out_24,
  output [7:0] out_25,
  output [7:0] out_26,
  output [7:0] out_27,
  output [7:0] out_28,
  output [7:0] out_29,
  output [7:0] out_30,
  output [7:0] out_31,
  output [7:0] out_32
);

  Comparador comparador_1 (.in_1(A), .in_2(B), .out_3(out_17), .out_4(out_18));
  Comparador comparador_2 (.in_1(C), .in_2(D), .out_3(out_19), .out_4(out_20));
  Comparador comparador_3 (.in_1(E), .in_2(F), .out_3(out_21), .out_4(out_22));
  Comparador comparador_4 (.in_1(G), .in_2(H), .out_3(out_23), .out_4(out_24));
  Comparador comparador_5 (.in_1(I), .in_2(J), .out_3(out_25), .out_4(out_26));
  Comparador comparador_6 (.in_1(K), .in_2(L), .out_3(out_27), .out_4(out_28));
  Comparador comparador_7 (.in_1(M), .in_2(N), .out_3(out_29), .out_4(out_30));
  Comparador comparador_8 (.in_1(O), .in_2(P), .out_3(out_31), .out_4(out_32));
endmodule

module HallAdder (
  input  A,
  input  B,
  output S,
  output C
);

  xor xor_1 (S, A, B);
  and and_1 (C, A, B);
endmodule

module FullAdder (
  input  A,
  input  B,
  input  Cin,
  output S,
  output Cout
);

  wire halladder_1_c, halladder_1_s, halladder_2_c;

  HallAdder halladder_1 (.A(A), .B(B), .S(halladder_1_s), .C(halladder_1_c));
  HallAdder halladder_2 (.A(halladder_1_s), .B(Cin), .S(S), .C(halladder_2_c));
  or or_1 (Cout, halladder_2_c, halladder_1_c);
endmodule

module Sumar1Bit (
  input  [1:0] FASE,
  input  Sumar1,
  output [2:0] out_3
);

  wire fulladder_1_cout;

  FullAdder fulladder_1 (.A(FASE[0]), .Cin(Sumar1), .S(out_3[0]), .Cout(fulladder_1_cout));  // open: B
  FullAdder fulladder_2 (.A(FASE[1]), .Cin(fulladder_1_cout), .S(out_3[1]), .Cout(out_3[2]));  // open: B
endmodule

module CompararRegistrar (
  input  [7:0] A,
  input  [7:0] B,
  input  [7:0] C,
  input  [7:0] D,
  input  [7:0] E,
  input  [7:0] F,
  input  [7:0] G,
  input  [7:0] H,
  input  [7:0] I,
  input  [7:0] J,
  input  [7:0] K,
  input  [7:0] L,
  input  [7:0] M,
  input  [7:0] N,
  input  [7:0] O,
  input  [7:0] P,
  input  CLK,
  input  [1:0] FASE,
  output [7:0] out_19,
  output [7:0] out_20,
  output [7:0] out_21,
  output [7:0] out_22,
  output [7:0] out_23,
  output [7:0] out_24,
  output [7:0] out_25,
  output [7:0] out_26,
  output [7:0] out_27,
  output [7:0] out_28,
  output [7:0] out_29,
  output [7:0] out_30,
  output [7:0] out_31,
  output [7:0] out_32,
  output [7:0] out_33,
  output [7:0] out_34
);

  wire [7:0] A1, B1, C1, D1, E1, F1, G1, H1, I1, J1, K1, L1, M1, multiplexer_1_out, multiplexer_2_out,
       multiplexer_3_out, multiplexer_4_out, multiplexer_5_out, multiplexer_6_out, multiplexer_7_out,
       multiplexer_8_out, multiplexer_9_out, multiplexer_10_out, multiplexer_11_out, multiplexer_12_out,
       multiplexer_13_out, multiplexer_14_out, multiplexer_15_out, multiplexer_16_out, N1, O1, P1;

  Multiplexer #(.select(2), .width(8)) multiplexer_1 (
    .in0(C), .in1(C1), .in2(C1), .in3(C1), .out(multiplexer_1_out), .sel(FASE));
  Multiplexer #(.select(2), .width(8)) multiplexer_2 (
    .in0(F), .in1(F1), .in2(F1), .in3(F1), .out(multiplexer_2_out), .sel(FASE));
  Multiplexer #(.select(2), .width(8)) multiplexer_3 (
    .in0(I), .in1(I1), .in2(I1), .in3(I1), .out(multiplexer_3_out), .sel(FASE));
  Multiplexer #(.select(2), .width(8)) multiplexer_4 (
    .in0(L), .in1(L1), .in2(L1), .in3(L1), .out(multiplexer_4_out), .sel(FASE));
  Multiplexer #(.select(2), .width(8)) multiplexer_5 (
    .in0(O), .in1(O1), .in2(O1), .in3(O1), .out(multiplexer_5_out), .sel(FASE));
  Multiplexer #(.select(2), .width(8)) multiplexer_6 (
    .in0(B), .in1(B1), .in2(B1), .in3(B1), .out(multiplexer_6_out), .sel(FASE));
  Multiplexer #(.select(2), .width(8)) multiplexer_7 (
    .in0(E), .in1(E1), .in2(E1), .in3(E1), .out(multiplexer_7_out), .sel(FASE));
  Multiplexer #(.select(2), .width(8)) multiplexer_8 (
    .in0(H), .in1(H1), .in2(H1), .in3(H1), .out(multiplexer_8_out), .sel(FASE));
  Multiplexer #(.select(2), .width(8)) multiplexer_9 (
    .in0(K), .in1(K1), .in2(K1), .in3(K1), .out(multiplexer_9_out), .sel(FASE));
  Multiplexer #(.select(2), .width(8)) multiplexer_10 (
    .in0(N), .in1(N1), .in2(N1), .in3(N1), .out(multiplexer_10_out), .sel(FASE));
  Multiplexer #(.select(2), .width(8)) multiplexer_11 (
    .in0(A), .in1(A1), .in2(A1), .in3(A1), .out(multiplexer_11_out), .sel(FASE));
  Multiplexer #(.select(2), .width(8)) multiplexer_12 (
    .in0(D), .in1(D1), .in2(D1), .in3(D1), .out(multiplexer_12_out), .sel(FASE));
  Multiplexer #(.select(2), .width(8)) multiplexer_13 (
    .in0(G), .in1(G1), .in2(G1), .in3(G1), .out(multiplexer_13_out), .sel(FASE));
  Multiplexer #(.select(2), .width(8)) multiplexer_14 (
    .in0(J), .in1(J1), .in2(J1), .in3(J1), .out(multiplexer_14_out), .sel(FASE));
  Multiplexer #(.select(2), .width(8)) multiplexer_15 (
    .in0(M), .in1(M1), .in2(M1), .in3(M1), .out(multiplexer_15_out), .sel(FASE));
  Multiplexer #(.select(2), .width(8)) multiplexer_16 (
    .in0(P), .in1(P1), .in2(P1), .in3(P1), .out(multiplexer_16_out), .sel(FASE));
  Comparar16Num comparar16num_1 (
    .A(multiplexer_11_out), .B(multiplexer_6_out), .C(multiplexer_1_out), .D(multiplexer_12_out),
    .E(multiplexer_7_out), .F(multiplexer_2_out), .G(multiplexer_13_out), .H(multiplexer_8_out),
    .I(multiplexer_3_out), .J(multiplexer_14_out), .K(multiplexer_9_out), .L(multiplexer_4_out),
    .M(multiplexer_15_out), .N(multiplexer_10_out), .O(multiplexer_5_out), .P(multiplexer_16_out),
    .out_17(out_19), .out_18(out_20), .out_19(out_21), .out_20(out_22), .out_21(out_23), .out_22(out_24),
    .out_23(out_25), .out_24(out_26), .out_25(out_27), .out_26(out_28), .out_27(out_29), .out_28(out_30),
    .out_29(out_31), .out_30(out_32), .out_31(out_33), .out_32(out_34));
  Registro8Bits registro8bits_1 (.NumReg(out_19), .CLK(CLK), .out_3(A1));
  Registro8Bits registro8bits_2 (.NumReg(out_20), .CLK(CLK), .out_3(I1));
  Registro8Bits registro8bits_3 (.NumReg(out_21), .CLK(CLK), .out_3(B1));
  Registro8Bits registro8bits_4 (.NumReg(out_22), .CLK(CLK), .out_3(J1));
  Registro8Bits registro8bits_5 (.NumReg(out_23), .CLK(CLK), .out_3(C1));
  Registro8Bits registro8bits_6 (.NumReg(out_24), .CLK(CLK), .out_3(K1));
  Registro8Bits registro8bits_7 (.NumReg(out_25), .CLK(CLK), .out_3(D1));
  Registro8Bits registro8bits_8 (.NumReg(out_26), .CLK(CLK), .out_3(L1));
  Registro8Bits registro8bits_9 (.NumReg(out_27), .CLK(CLK), .out_3(E1));
  Registro8Bits registro8bits_10 (.NumReg(out_28), .CLK(CLK), .out_3(M1));
  Registro8Bits registro8bits_11 (.NumReg(out_29), .CLK(CLK), .out_3(F1));
  Registro8Bits registro8bits_12 (.NumReg(out_30), .CLK(CLK), .out_3(N1));
  Registro8Bits registro8bits_13 (.NumReg(out_31), .CLK(CLK), .out_3(G1));
  Registro8Bits registro8bits_14 (.NumReg(out_32), .CLK(CLK), .out_3(O1));
  Registro8Bits registro8bits_15 (.NumReg(out_33), .CLK(CLK), .out_3(H1));
  Registro8Bits registro8bits_16 (.NumReg(out_34), .CLK(CLK), .out_3(P1));
endmodule

module MaquinaEstados (
  input  X,
  input  CLK,
  input  CLEAR,
  output [1:0] FASE
);

  wire and_1_out, and_2_out, and_3_out, and_4_out, and_5_out, not_1_out, not_2_out, or_1_out;

  not not_1 (not_1_out, FASE[1]);
  not not_2 (not_2_out, FASE[0]);
  and and_1 (and_1_out, X, not_1_out, FASE[0]);
  and and_2 (and_2_out, FASE[1], FASE[0]);
  and and_3 (and_3_out, X, not_2_out);
  and and_4 (and_4_out, FASE[1], FASE[0]);
  and and_5 (and_5_out, X, FASE[0]);
  or or_1 (or_1_out, and_4_out, and_5_out);
  S_R_Flip_Flop s_r_ff_1 (.S(and_1_out), .R(and_2_out), .clk(CLK), .Q(FASE[1]), .reset(CLEAR));  // open: Qn, preset
  S_R_Flip_Flop s_r_ff_2 (.S(and_3_out), .R(or_1_out), .clk(CLK), .Q(FASE[0]), .reset(CLEAR));  // open: Qn, preset

  // Other names for the same wires on the sheet: Q0 = FASE[0]; Q1 = FASE[1]
endmodule
